// Digital circuit CPU8Bit32i.dig as structural Verilog
module CPU8Bit32i (
  input  RST,
  input  Clock,
  input  [7:0] BusIn,
  input  [7:0] PromIN,
  input  [7:0] RamIn,
  output [7:0] BusOut,
  output [7:0] AddrBus,
  output OutE,
  output [7:0] PCaddr,
  output RamE
);

  wire AE, and_1_out, BE, BMux0, BMux1, C, CE, Cout, E, G, IRZ, JMP, multiplexer_1_out, N, OP0, OP1, OP2,
       OP3, PcASel, S, Z;
  wire [4:0] IR;
  wire [7:0] A_q, alu8bits8f_1_y, B, PC;

  Control control_1 (
    .in(IR), .CLK(Clock), ._0(BMux0), ._1(BMux1), ._2(PcASel), ._3(IRZ), ._4(RamE), ._5(OP0), ._6(OP1),
    ._7(OP2), ._8(OP3), ._9(JMP), ._10(OutE), ._11(AE), ._12(BE), ._13(CE));
  Multiplexer #(.Selector_Bits(3)) multiplexer_1 (
    .sel({OP2, OP1, OP0}), .in_0(1'b0), .in_1(1'b1), .in_2(Z), .in_3(E), .in_4(G), .in_5(S), .in_6(N),
    .in_7(C), .out(multiplexer_1_out));
  Reg5 u_IR (.D(PromIN[4:0]), .Q(IR), .SR(IRZ), .nCLK(Clock));
  and and_1 (and_1_out, multiplexer_1_out, JMP);
  Reg8 A (.E(AE), .CLK(Clock), .D(BusOut), .Q(A_q));
  ALU8Bits8f alu8bits8f_1 (
    .Y(alu8bits8f_1_y), .A(A_q), .B(B), .ST({Cout, N, S, G, E, Z}), .OPC({C, OP3, OP2, OP1, OP0}));
  PC u_PC (.L(and_1_out), .R(RST), .nCLK(Clock), .D(BusOut), .Q(PC));
  Register register_1 (.D(Cout), .C(Clock), .en(CE), .Q(C));
  Reg8 u_B (.E(BE), .CLK(Clock), .D(BusOut), .Q(B));
  Multiplexer #(.Selector_Bits(2), .Bits(8)) multiplexer_2 (
    .sel({BMux1, BMux0}), .in_0(alu8bits8f_1_y), .in_1(RamIn), .in_2(BusIn), .in_3(PromIN), .out(BusOut));
  Multiplexer #(.Bits(8)) multiplexer_3 (.sel(IRZ), .in_0(B), .in_1(PromIN), .out(AddrBus));
  Multiplexer #(.Bits(8)) multiplexer_4 (.sel(PcASel), .in_0(B), .in_1(PC), .out(PCaddr));

  // Other names for the same wires on the sheet: BUS[7:0] = BusOut; CLK = Clock; PROM[7:0] = PromIN; RESET = RST

  // Notes on the sheet:
  //   RST: default 1
  //   Clock: Hz: 10
endmodule
