// Digital circuit CPU8Bit32iTESTE.dig as structural Verilog
module CPU8Bit32iTESTE (
  input  RST,
  input  Clock,
  input  [7:0] BusIn,
  input  [7:0] PromIN,
  input  [7:0] RamIn,
  input  Dip4,
  input  Dip1,
  input  Dip2,
  input  Dip3,
  input  S1,
  input  S2,
  input  S3,
  input  reserv,
  output [7:0] BusOut,
  output [7:0] AddrBus,
  output OutE,
  output [7:0] PCaddr,
  output RamE,
  output [7:0] out0,
  output [7:0] out1,
  output [7:0] A,
  output [7:0] B,
  output C,
  output [4:0] IR,
  output [7:0] PC
);

  wire AE, and_1_out, and_2_out, and_3_out, and_4_out, BE, BusMux0, BusMux1, BusMux2, CCLR, CE, Cout, CSET,
       E, G, IRZ, JMP, multiplexer_1_out, N, not_1_out, OP0, OP1, OP2, RamAMux, S, Z;
  wire [7:0] alu8bits8f_1_y, ctrlrom_1_p3, PROM;

  ROM #(.AddrBits(8), .Bits(8)) rom_1 (.A(PCaddr), .sel(1'b1), .D(PROM));
  Multiplexer #(.Selector_Bits(3)) multiplexer_1 (
    .sel({OP2, OP1, OP0}), .in_0(1'b0), .in_1(1'b1), .in_2(Z), .in_3(E), .in_4(G), .in_5(S), .in_6(N),
    .in_7(C), .out(multiplexer_1_out));
  // CtrlRom ctrlrom_1: pin names not known; wires that end beside it: RamIn, IR, ctrlrom_1_p3, BusMux0, BusMux1, BusMux2, IRZ, RamAMux, RamE, OP0, OP1, OP2, JMP, OutE, AE, BE, CSET, CE, CCLR, BusOut
  and and_1 (and_1_out, JMP, multiplexer_1_out);
  PC u_PC (.L(and_1_out), .R(RST), .nCLK(Clock), .D(BusOut), .Q(PC));
  Reg8 u_A (.E(AE), .CLK(Clock), .D(BusOut), .Q(A));
  Reg1 u_C (.Q(C), .CLR(CCLR), .S(CSET), .D(Cout), .CLK(Clock), .E(CE));
  ALU8Bits8f alu8bits8f_1 (.Y(alu8bits8f_1_y), .A(A), .B(B), .ST({Cout, N, S, G, E, Z}), .OPC({C, OP2, OP1, OP0}));
  Reg5 u_IR (.D(PROM[4:0]), .Q(IR), .SR(IRZ), .nCLK(Clock));
  Reg8 u_B (.E(BE), .CLK(Clock), .D(BusOut), .Q(B));
  Multiplexer #(.Selector_Bits(3), .Bits(8)) multiplexer_2 (
    .sel({BusMux2, BusMux1, BusMux0}), .in_0(alu8bits8f_1_y), .in_1(ctrlrom_1_p3),
    .in_2({reserv, S3, S2, S1, Dip1, Dip2, Dip3, Dip4}), .in_3(PROM), .in_4(A), .in_5(B), .in_6(PROM),
    .in_7({8{1'b0}}), .out(BusOut));
  Multiplexer #(.Bits(8)) multiplexer_3 (.sel(RamAMux), .in_0(B), .in_1(PROM), .out(AddrBus));
  and and_2 (and_2_out, BusMux1, BusMux2, ~Clock);  // And
  Multiplexer #(.Bits(8)) multiplexer_4 (.sel(and_2_out), .in_0(PC), .in_1(B), .out(PCaddr));
  not not_1 (not_1_out, AddrBus[0]);
  and and_3 (and_3_out, not_1_out, OutE);
  and and_4 (and_4_out, AddrBus[0], OutE);
  RAMDualPort #(.Bits(8)) ramdualport_1 (
    .A(AddrBus[1:0]), .Din(BusOut), .str(RamE), .C(Clock), .ld(1'b1), .D(ctrlrom_1_p3));
  Register #(.Bits(8)) register_1 (.D(BusOut), .C(Clock), .en(and_3_out), .Q(out0));
  Register #(.Bits(8)) register_2 (.D(BusOut), .C(Clock), .en(and_4_out), .Q(out1));
  LED led_1 (.in(out0[0]));
  LED led_2 (.in(out0[1]));
  Seven_Seg seven_seg_1 (
    .a(out1[0]), .b(out1[1]), .c(out1[2]), .d(out1[3]), .e(out1[4]), .f(out1[5]), .g(out1[6]), .dp(out1[7]));

  // Other names for the same wires on the sheet: BUS[7:0] = BusOut; CLK = Clock; a_t = out1[0]; b_t = out1[1];
  //   c_t = out1[2]; d = out1[3]; e_t = out1[4]; f = out1[5]; g_t = out1[6]; dp = out1[7]; RESET = RST

  // Notes on the sheet:
  //   RST: default 1
  //   Clock: Hz: 200
  //   out0: pin 67,68,78,82,84,86,88,90
  //   out1: pin 75,73,71,70,72,76,74,69
  //   Dip4: pin 58
  //   Dip1: pin 61
  //   Dip2: pin 66
  //   Dip3: pin 57
  //   S1: pin 54
  //   S2: pin 56
  //   S3: pin 55
  //   reserv: pin 100
  //   contents of rom_1 (hex, n*v repeats v):
  //   c,0,7,0,2,f,1a,7,1,a,0,1f,17,1f,17,1f,17,1f,d,0,2,3,12,1c,f,22
  //   ,f,0,1,40,d,1,f,0,a,1,2,2d,1c,4,3,d,1,f,1a,3f,6,5b,4f,66,6d,7d
  //   ,7,7f,6f,77,7c,39,5e,79,71
endmodule
