// Digital circuit ALU8Bits8f.dig as structural Verilog
module ALU8Bits8f (
  input  [7:0] A,
  input  [7:0] B,
  input  [3:0] OPC,
  output [7:0] Y,
  output [5:0] ST
);

  wire add_1_c_o, lsl8_1_co, lsr8_1_co, sub_1_c_o;
  wire [7:0] add_1_s, and_1_out, lsl8_1_do, lsr8_1_do, not_1_out, or_1_out, sub_1_s, xor_1_out;

  Comparator #(.Signed("true"), .Bits(8)) comparator_1 (.a(A), .b({8{1'b0}}), .eq(ST[0]));  // open: gt, lt
  Comparator #(.Signed("true"), .Bits(8)) comparator_2 (.a(A), .b(B), .gt(ST[2]), .eq(ST[1]), .lt(ST[3]));
  assign not_1_out = ~A;  // Not not_1, 8 bits wide
  assign or_1_out = A | B;  // Or or_1, 8 bits wide
  assign and_1_out = A & B;  // And and_1, 8 bits wide
  assign xor_1_out = A ^ B;  // XOr xor_1, 8 bits wide
  Add #(.Bits(8)) add_1 (.a(A), .b(B), .c_i(OPC[3]), .s(add_1_s), .c_o(add_1_c_o));
  Sub #(.Bits(8)) sub_1 (.a(A), .b(B), .c_i(OPC[3]), .s(sub_1_s), .c_o(sub_1_c_o));
  LSL8 lsl8_1 (.Di(A), .Ci(OPC[3]), .Do(lsl8_1_do), .Co(lsl8_1_co));
  LSR8 lsr8_1 (.Di(A), .Ci(OPC[3]), .Do(lsr8_1_do), .Co(lsr8_1_co));
  Multiplexer #(.Selector_Bits(3), .Bits(8)) multiplexer_1 (
    .sel(OPC[2:0]), .in_0(not_1_out), .in_1(or_1_out), .in_2(and_1_out), .in_3(xor_1_out), .in_4(add_1_s),
    .in_5(sub_1_s), .in_6(lsl8_1_do), .in_7(lsr8_1_do), .out(Y));
  Multiplexer #(.Selector_Bits(2)) multiplexer_2 (
    .sel(OPC[1:0]), .in_0(add_1_c_o), .in_1(sub_1_c_o), .in_2(lsl8_1_co), .in_3(lsr8_1_co), .out(ST[5]));

  assign ST[4] = A[7];

  // Other names for the same wires on the sheet: N = A[7]; C = ST[5]; E = ST[1]; G = ST[2]; OP[2:0] = OPC[2:0];
  //   S = ST[3]; Z = ST[0]
endmodule
